// Logisim project RV32_IM.circ as structural Verilog: 2 circuits, main circuit main
module main (
);

  wire W_EN;
  wire [31:0] ADDR, DATA, INST;

  Clock clock_1 (.out(W_EN));
  CPU cpu_1 (.in_1(INST), .in_2(W_EN), .out_3(ADDR), .out_4(DATA), .out_5(W_EN));
  RAM #(.addrWidth(24), .dataWidth(32), .enables("line")) ram_1 (
    .addr(ADDR[23:0]), .we(W_EN), .clk(W_EN), .din(DATA), .dout(INST));
endmodule

module CPU (
  input  [31:0] in_1,
  input  in_2,
  output [31:0] out_3,
  output [31:0] out_4,
  output out_5
);

  wire B_TYPE, I_TYPE, I_TYPE_JUMP, I_TYPE_LOAD, R_TYPE, U_TYPE_JUMP, U_TYPE_LOAD;
  wire [31:0] PC_1;

  Register #(.width(32)) PC (.D(PC_1), .en(in_2), .clk(in_2), .Q(out_3));  // open: clr
  Adder #(.width(32)) adder_1 (.a(out_3), .b(32'h1), .out(PC_1));  // open: cin, cout
  Comparator #(.width(7)) comparator_1 (.a(in_1[6:0]), .b(7'b0110011), .eq(R_TYPE));  // open: gt, lt
  Comparator #(.width(7)) comparator_2 (.a(in_1[6:0]), .b(7'b0000011), .eq(I_TYPE_LOAD));  // open: gt, lt
  Comparator #(.width(7)) comparator_3 (.a(in_1[6:0]), .b(7'b0010011), .eq(I_TYPE));  // open: gt, lt
  Comparator #(.width(7)) comparator_4 (.a(in_1[6:0]), .b(7'b0100011), .eq(R_TYPE));  // open: gt, lt
  Comparator #(.width(7)) comparator_5 (.a(in_1[6:0]), .b(7'b1100011), .eq(B_TYPE));  // open: gt, lt
  Comparator #(.width(7)) comparator_6 (.a(in_1[6:0]), .b(7'b0110111), .eq(U_TYPE_LOAD));  // open: gt, lt
  Comparator #(.width(7)) comparator_7 (.a(in_1[6:0]), .b(7'b1100111), .eq(U_TYPE_JUMP));  // open: gt, lt
  Comparator #(.width(7)) comparator_8 (.a(in_1[6:0]), .b(7'b1101111), .eq(I_TYPE_JUMP));  // open: gt, lt

  // Other names for the same wires on the sheet: CLK = in_2; PC[31:0] = out_3; RAM_ADDR[31:0] = out_3;
  //   RAM_DATA[31:0] = out_4; OPCODE[6:0] = in_1[6:0]; RAM_INSTRUCTION[31:0] = in_1; IMM_11_B = in_1[7];
  //   RD[4:0] = in_1[11:7]; IMM_4_1[3:0] = in_1[11:8]; FUNCT3[2:0] = in_1[14:12]; IMM_19_12[7:0] = in_1[19:12];
  //   IMM_31_12[19:0] = in_1[31:12]; RS1[4:0] = in_1[19:15]; IMM_11_0[11:0] = in_1[31:20]; IMM_11_J = in_1[20];
  //   RS2[4:0] = in_1[24:20]; IMM_10_1[8:0] = in_1[29:21]; FUNCT7[6:0] = in_1[31:25]; IMM_10_5[5:0] = in_1[30:25];
  //   IMM_11_5[5:0] = in_1[31:26]; IMM_20[1:0] = in_1[31:30]; IMM_12 = in_1[31]; RAM_WRITE_EN = out_5

  // Notes on the sheet:
  //   outputs
  //   I/O
  //   FETCH
  //   inputs
  //   R-Type
  //   I-Type
  //   U-Type
  //   S-Type
  //   B-Type
  //   J-Type
  //   IMM_4_0
  //   DECODE
endmodule
